// Logisim project 1_zadanie.circ as structural Verilog: 1 circuit, main circuit main
module main (
  input  A,
  input  B,
  input  C,
  input  D,
  output Y_zad,
  output Z_zad,
  output Y_DNF,
  output Z_DNF,
  output Y_KNF,
  output Z_KNF
);

  wire A_B_C_nD_out, A_nB_D_out, A_nB_nC_out, A_nB_nCD_out, AB_nD_out, ABC_out, B_D_out, n_A_B_out,
       n_C_nD_out, nA_2_out, nA_B_D_out, nA_B_nC_out, nA_nB_C_nD_out, nA_nB_nD_out, nA_nBC_out, nA_out,
       nAB_nCD_out, nB_2_out, nB_out, nC_2_out, nC_out, nD_2_out, nD_3_out, nD_out;

  not nA (nA_out, A);
  not nB (nB_out, B);
  not nD (nD_out, D);
  not nC (nC_out, C);
  not nA_2 (nA_2_out, A);
  not nC_2 (nC_2_out, C);
  not nB_2 (nB_2_out, B);
  not nD_2 (nD_2_out, D);
  not nD_3 (nD_3_out, D);
  xnor n_A_B (n_A_B_out, A, B);
  nor n_C_nD (n_C_nD_out, C, nD_3_out);
  or B_D (B_D_out, B, D);
  and ABC (ABC_out, A, B, C);
  and nA_nB_nD (nA_nB_nD_out, nA_out, nB_out, nD_out);
  and AB_nD (AB_nD_out, A, B, nD_out);
  and nA_nBC (nA_nBC_out, nA_out, nB_out, C);
  and A_nB_nCD (A_nB_nCD_out, A, nB_out, nC_out, D);
  and nAB_nCD (nAB_nCD_out, nA_out, B, nC_out, D);
  or nA_B_nC (nA_B_nC_out, nA_2_out, B, nC_2_out);
  or nA_B_D (nA_B_D_out, nA_2_out, B, D);
  or A_nB_nC (A_nB_nC_out, A, nB_2_out, nC_2_out);
  or A_nB_D (A_nB_D_out, A, nB_2_out, D);
  or A_B_C_nD (A_B_C_nD_out, A, B, C, nD_2_out);
  or nA_nB_C_nD (nA_nB_C_nD_out, nA_2_out, nB_2_out, C, nD_2_out);
  or C_nD (Z_KNF, C, nD_2_out);
  xor n_A_B__n_C_nD (Y_zad, n_A_B_out, n_C_nD_out);
  nand n_n_C_nD___B_D (Z_zad, n_C_nD_out, B_D_out);
  or \or  (Y_DNF, ABC_out, nA_nB_nD_out, AB_nD_out, nA_nBC_out, A_nB_nCD_out, nAB_nCD_out);
  or C_nD_2 (Z_DNF, C, nD_out);
  and \and  (Y_KNF, nA_B_nC_out, nA_B_D_out, A_nB_nC_out, A_nB_D_out, A_B_C_nD_out, nA_nB_C_nD_out);
endmodule
