// Logisim project 2_zadanie.circ as structural Verilog: 1 circuit, main circuit main
module main (
  input  a,
  input  b,
  input  c,
  input  d,
  output A_D,
  output B_D,
  output C_D,
  output D_D,
  output A_K,
  output B_K,
  output C_K,
  output D_K
);

  wire a__nb_out, a__nc_out, a_c_out, b__nd_out, b_d_out, c__nd_out, c_d_out, na_2_out, na___nc_out,
       na__c_out, na_out, nb_2_out, nb___nd_out, nb__d_out, nb_out, nc_2_out, nc___nd_out, nc__d_out, nc_out,
       nd_2_out, nd_out;

  nand na (na_out, a, a);
  nor na_2 (na_2_out, a, a);
  nand nc (nc_out, c, c);
  nand nb (nb_out, b, b);
  nor nc_2 (nc_2_out, c, c);
  nor nb_2 (nb_2_out, b, b);
  nand nd (nd_out, d, d);
  nor nd_2 (nd_2_out, d, d);
  nand a__nb (a__nb_out, a, nb_out);
  nand c__nd (c__nd_out, c, nd_out);
  nand nc__d (nc__d_out, nc_out, d);
  nand a__nc (a__nc_out, a, nc_out);
  nand na__c (na__c_out, na_out, c);
  nand b__nd (b__nd_out, b, nd_out);
  nand nb__d (nb__d_out, nb_out, d);
  nor u_c_d (c_d_out, c, d);
  nor nc___nd (nc___nd_out, nc_2_out, nd_2_out);
  nor a_c (a_c_out, a, c);
  nor na___nc (na___nc_out, na_2_out, nc_2_out);
  nor u_b_d (b_d_out, b, d);
  nor nb___nd (nb___nd_out, nb_2_out, nd_2_out);
  nand a__nb____a__nb (A_D, a__nb_out, a__nb_out);
  nand c__nd_____nc__d (B_D, c__nd_out, nc__d_out);
  nand a__nc_____na__c (C_D, a__nc_out, na__c_out);
  nand b__nd_____nb__d (D_D, b__nd_out, nb__d_out);
  nor na__b (A_K, na_2_out, b);
  nor c_d____nc___nd (B_K, c_d_out, nc___nd_out);
  nor c_d____nc___nd_2 (C_K, a_c_out, na___nc_out);
  nor b_d____nb___nd (D_K, b_d_out, nb___nd_out);
endmodule
