// Logisim project 3_zadanie.circ as structural Verilog: 1 circuit, main circuit main
module main (
  input  X,
  input  Res,
  output Y
);

  wire CLK_out, j_k_ff_1_q, j_k_ff_1_qn, j_k_ff_2_q, j_k_ff_2_qn, j_k_ff_3_q, j_k_ff_3_qn, nx_nz2_out,
       nx_out, nx_z1_z3___nx_z1_z3_out, nx_z1_z3_out, nx_z2_z3___nx_z2_z3_out, nx_z2_z3_out, nz1_nz2_out,
       x__nz1_nz2_out, x__z1_nz2_out, x_nz1_out, x_nz1_z3_out, x_z1_z2_out, z1_nz2_out;

  nand nx (nx_out, X, X);
  Clock CLK (.out(CLK_out));
  nand x_z1_z2 (x_z1_z2_out, j_k_ff_1_q, j_k_ff_2_q, X);
  nand nx_z2_z3 (nx_z2_z3_out, nx_out, j_k_ff_2_q, j_k_ff_3_q);
  nand nx_z1_z3 (nx_z1_z3_out, nx_out, j_k_ff_1_q, j_k_ff_3_q);
  nand x_nz1_z3 (x_nz1_z3_out, X, j_k_ff_1_qn, j_k_ff_3_q);
  nand z1_nz2 (z1_nz2_out, j_k_ff_1_q, j_k_ff_2_qn);
  nand nz1_nz2 (nz1_nz2_out, j_k_ff_1_qn, j_k_ff_2_qn);
  nand nx_z2_z3___nx_z2_z3 (nx_z2_z3___nx_z2_z3_out, nx_z2_z3_out, nx_z2_z3_out);
  nand nx_nz2 (nx_nz2_out, nx_out, j_k_ff_2_qn);
  nand nx_z1_z3___nx_z1_z3 (nx_z1_z3___nx_z1_z3_out, nx_z1_z3_out, x_nz1_z3_out);
  nand x_nz1 (x_nz1_out, X, j_k_ff_1_qn);
  nand x__z1_nz2 (x__z1_nz2_out, nx_out, z1_nz2_out);
  nand x__nz1_nz2 (x__nz1_nz2_out, X, nz1_nz2_out);
  nand x_z1_z2___x_z1_z2 (Y, x_z1_z2_out, x_z1_z2_out);
  J_K_Flip_Flop j_k_ff_1 (
    .J(nx_z2_z3___nx_z2_z3_out), .clk(CLK_out), .K(nx_nz2_out), .Q(j_k_ff_1_q), .Qn(j_k_ff_1_qn), .reset(Res));  // open: preset, en
  J_K_Flip_Flop j_k_ff_2 (
    .J(nx_z1_z3___nx_z1_z3_out), .clk(CLK_out), .K(x_nz1_out), .Q(j_k_ff_2_q), .Qn(j_k_ff_2_qn), .reset(Res));  // open: preset, en
  J_K_Flip_Flop j_k_ff_3 (
    .J(x__z1_nz2_out), .clk(CLK_out), .K(x__nz1_nz2_out), .Q(j_k_ff_3_q), .Qn(j_k_ff_3_qn), .reset(Res));  // open: preset, en

  // Notes on the sheet:
  //   z1
  //   z2
  //   z3
endmodule
